// Logisim project full adder using or gate.circ as structural Verilog: 1 circuit, main circuit main
module main (
  input  in_1,
  input  in_2,
  output out_3,
  output out_4
);

  wire or_1_out, or_2_out, or_3_out;

  or or_1 (or_1_out, in_1, in_2);
  or or_2 (or_2_out, in_1, in_1);
  or or_3 (or_3_out, in_2, in_2);
  nor nor_1 (out_3, or_2_out, or_3_out);
  nor nor_2 (out_4, out_3, or_1_out);
endmodule
